# Fritzing sketch Schematic (saved by Fritzing 0.9.3b)
circuit board: 14.9152cm x 11.3347cm
breadboards: 1

parts:
  hc-sr1 = hc-sr04
  RTC_DS3231 = ZS-042 RTC Module
  Servo = Basic Servo
  Relay = 2-Channel 5v Relay Shield [package=relay-2ch5v10a]
  LED1 = LEDs [package=led10mm]
  Fan = Fan - Ventilador [package=THT]
  NodeMCU = NodeMCU V3.0
  DHT1 = DHT11 Humitidy and Temperature Sensor (3 pins)
  External_Voltage = female pin header, 2 pins [form="♀ (female)"]

nets (from the breadboard view):
  VCC: hc-sr1.VCC, RTC_DS3231.VCC, Servo.vcc, NodeMCU.3V3, DHT1.Signal
  N1: hc-sr1.Trig, NodeMCU.D6
  N2: hc-sr1.Echo, NodeMCU.D7
  GND: hc-sr1.GND, RTC_DS3231.GND, Servo.gnd, NodeMCU.GND, DHT1.GND, External_Voltage.pin1
  N3: RTC_DS3231.SDA, NodeMCU.D1
  N4: RTC_DS3231.SCL, NodeMCU.D2
  N5: Servo.pulse, NodeMCU.D5
  N6: Relay.VCC, Relay.K1-On, Relay.K2-On
  GND_2: Relay.GND, Relay.IN1, Relay.K1-Off, Relay.K2-Off, LED1.C, Fan.GND
  N7: Relay.K1-In, Fan.5V
  N8: Relay.K2-In, LED1.A
  N9: NodeMCU.RX, DHT1.VDD
  N10: NodeMCU.Vin, External_Voltage.pin2

custom parts:
  2-Channel 5v Relay Shield: 2 Channel 5v Relay Shield w. 2x SPD-06VDC-SD-C
  Fan - Ventilador: Ventilador de 2 pines, se encuentra comunmente en computadoras de escritorio
  NodeMCU V3.0: ESP8266 based NodeMCU
  DHT11 Humitidy and Temperature Sensor (3 pins): DHT11 Humidity and Temperature Sensor (3 pins) from the design created by John De Cristofaro for Adafruit Industries.
